# Fritzing sketch IRPhoneCamera (saved by Fritzing 0.7.7b)
breadboards: 1

parts:
  C1 = Ceramic Capacitor [capacitance=0.1µF package="100 mil [THT, multilayer]"]
  MLX90614_Infrared_Thermometer1 = MLX90614 Infrared Thermometer
  R1 = Resistor [tolerance=±5% resistance=4.7k package=THT]
  R2 = Resistor [tolerance=±5% resistance=4.7k package=THT]
  D1 = Rectifier Diode [part_number=1N4001 breakdown_voltage=3.6V package="300 mil [THT]"]
  D2 = Rectifier Diode [part_number=1N4001 package="300 mil [THT]"]
  S1 = Toggle Switch [package=THT]
  C4 = Electrolytic Capacitor [capacitance=10µF voltage=20V package="100 mil [THT, electrolytic]"]
  C5 = Electrolytic Capacitor [capacitance=10µF voltage=20V package="100 mil [THT, electrolytic]"]
  U1 = Voltage Regulator -- 3.3 V -- LM1117
  J1 = female pin header, 17 pins [form="♀ (female)"]
  J2 = female pin header, 17 pins [form="♀ (female)"]
  J3 = female pin header, 12 pins [form="♀ (female)"]
  J4 = female pin header, 12 pins [form="♀ (female)"]
  + = female pin header, 2 pins [form="♀ (female)"]
  Part1 = Arduino Pro Mini 3.3V

nets:
  VSS: C1.0, MLX90614_Infrared_Thermometer1.VSS, C4.-, C5.-, U1.GND, J1.pin16, J1.pin17, J4.pin2, +.pin2, Part1.GND#23
  N1: C1.1, MLX90614_Infrared_Thermometer1.VDD, D1.cathode
  N2: MLX90614_Infrared_Thermometer1.PWM_/_SDA, R1.Pin_0, Part1.A4
  N3: MLX90614_Infrared_Thermometer1.SCL_/_Vz, R2.Pin_0, Part1.A5
  N4: R1.Pin_1, R2.Pin_1, D1.anode, C5.+, U1.OUT, J1.pin14, J1.pin15, J4.pin4, Part1.VCC
  N5: D2.cathode, C4.+, U1.IN
  N6: D2.anode, S1.L2
  N7: S1.COM, +.pin1
  N8: J2.pin12, J3.pin6, Part1.D3
  N9: J2.pin13, J3.pin5, Part1.D2
  N10: J3.pin1, Part1.TXO
  N11: J3.pin2, Part1.RXI
  N12: J3.pin3, Part1.RESET#43
  N13: J3.pin4, Part1.GND#42
  N14: J3.pin7, Part1.D4
  N15: J3.pin8, Part1.D5
  N16: J3.pin9, Part1.D6
  N17: J3.pin10, Part1.D7
  N18: J3.pin11, Part1.D8
  N19: J3.pin12, Part1.D9
  N20: J4.pin1, Part1.RAW
  N21: J4.pin3, Part1.RESET#24
  N22: J4.pin5, Part1.A3
  N23: J4.pin6, Part1.A2
  N24: J4.pin7, Part1.A1
  N25: J4.pin8, Part1.A0
  N26: J4.pin9, Part1.SCK
  N27: J4.pin10, Part1.MISO
  N28: J4.pin11, Part1.MOSI
  N29: J4.pin12, Part1.D10

notes:
  MLX90620
  3.3v Gnd
  WiFly RN-131g Breakout
  RX TX

custom parts:
  MLX90614 Infrared Thermometer: The MLX90614 is an Infra Red thermometer for non contact temperature measurements. Both the IR sensitive thermopile detector chip and the signal conditioning ASSP are integrated in the same TO-39 can.
  Voltage Regulator -- 3.3 V -- LM1117: LM1117-3.3 Voltage regulator, 3.3 V output. Note that the pinout order is not the same as LM7805 or LM7833.
  Arduino Pro Mini 3.3V: Description: It's blue! It's thin (0.8mm)! It's the Arduino Pro Mini! SparkFun's minimal design approach to Arduino. This is a 3.3V Arduino running the 8MHz bootloader (select 'Arduino Duemilanove w/ 328' within the Arduino software). Arduino Pro Mini does not come with connectors populated so that you can solder in any connector or wire with any orientation you need. We recommend first time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
